// Logisim project FinalProject.circ as structural Verilog: 1 circuit, main circuit main
module main (
  input  Reset_RAM,
  input  Manual_cycle,
  input  Reset
);

  wire Goto_enable, main_2_alu_enable, main_2_ram_read, main_2_ram_write, main_2_register_write;
  wire [1:0] main_1_p5;
  wire [3:0] main_2_opcode_to_alu;
  wire [7:0] Instruction_num;
  wire [31:0] alu_1_output, n16_register_file_1_a, n16_register_file_1_b, rom_1_data;

  ROM #(.dataWidth(32)) rom_1 (.addr(Instruction_num), .data(rom_1_data));  // open: sel
  // Clock_main main_1: pin names not known; wires that end beside it: Goto_enable, Manual_cycle, Reset, Instruction_num, main_1_p5
  _16_register_file u_16_register_file_1 (
    .d(alu_1_output), .Clk(main_2_register_write), .a(n16_register_file_1_a), .b(n16_register_file_1_b));  // open: Rd, Clr, Ra, Rb
  ALU alu_1 (
    .A(n16_register_file_1_a), .B(n16_register_file_1_b), .Op_code(main_2_opcode_to_alu),
    .in_5(main_2_alu_enable), .\output (alu_1_output));  // open: imm
  cliff_bus_control_11_07_15_main main_2 (
    .Cycle_LSB(main_1_p5[0]), .Cycle_MSB(main_1_p5[1]), .ALU_Enable(main_2_alu_enable),
    .Register_Write(main_2_register_write), .RAM_Read(main_2_ram_read), .RAM_Write(main_2_ram_write),
    .OPCode_to_ALU(main_2_opcode_to_alu), .Program_Counter_Update(Goto_enable));  // open: OP
  RAM #(.dataWidth(32), .bus("separate")) ram_1 (
    .data(alu_1_output), .str(main_2_ram_write), .ld(main_2_ram_read), .clr(Reset_RAM));  // open: addr, din, sel, clk

  // Notes on the sheet:
  //   ROM (Instructions)
  //   Clock
  //   Registers
  //   32-bit CPU
  //   By Cliff, Will, Tom, & Crissy
  //   ALU
  //   Bus Control
  //   RAM
endmodule
