// Logisim project Clock.circ as structural Verilog: 2 circuits, main circuit Test
module main (
  input  Reset,
  output [7:0] Counter,
  output [1:0] State
);

  wire and_1_out, not_1_out;
  wire [7:0] adder_1_out;

  Clock clock_1 (.out(State[0]));
  not not_1 (not_1_out, State[0]);
  and and_1 (and_1_out, State[0], State[1]);
  T_Flip_Flop t_ff_1 (.clk(not_1_out), .T(1'b1), .Q(State[1]), .reset(Reset));  // open: Qn, preset, en
  Adder adder_1 (.a(8'h1), .b(Counter), .out(adder_1_out));  // open: cin, cout
  Register u_Counter (.D(adder_1_out), .Q(Counter), .clk(and_1_out), .clr(Reset));  // open: en
endmodule

module Test (
  input  in_1,
  output [7:0] Counter,
  output [1:0] state
);

  main main_1 (.Reset(in_1), .Counter(Counter), .State(state));
endmodule
